# Fritzing sketch schematic (saved by Fritzing 0.9.3b)
circuit board: 7cm x 5cm
breadboards: 1

parts:
  Part1 = Adafruit Pro Trinket 3.3V 12MHz [part_number="Adafruit #2010"]
  Part2 = NRF24L01+ Breakout Board
  100kΩ = Resistor [tolerance=±5% resistance=100k package=THT]
  LDR = Photocell (LDR) [package=THT]
  4_7kΩ = Resistor [tolerance=±5% resistance=4.7k package=THT]
  DS1 = DS18B20 1-Wire Temperature Sensor [part_number=DS18B20]
  AM2302 = AM2302 Humidity and Temperature Sensor

nets:
  GND: Part1.GND, Part2.GND, 100kΩ.Pin_0, DS1.GND, AM2302.GND
  VDD: Part1.+3V3, Part2.VCC, LDR.pin_1, 4_7kΩ.Pin_1, DS1.VDD, AM2302.VDD
  N1: Part1.D4, AM2302.DATA
  N2: Part1.D3, DS1.DQ
  N3: Part1.D9, Part2.CE
  N4: Part1.D10, Part2.CS
  N5: Part1.D11, Part2.MOSI
  N6: Part1.D12, Part2.MISO
  N7: Part1.D13, Part2.SCK
  N8: Part1.A1, LDR.pin_0

custom parts:
  Adafruit Pro Trinket 3.3V 12MHz: rinket's got a big sister in town - the Pro Trinket 3V! Pro Trinket combines everything you love about Trinket with the familiarity of the core Arduino chip, the ATmega328. It's like an Arduino Pro Mini with more pins and USB tossed in. Trinket's a year old now, and while its been great to see tons of tiny projects, sometimes you just need more pins, more FLASH, and more RAM. That's why we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
